# Fritzing sketch edison_schematics (saved by Fritzing 0.9.3b)
breadboards: 1

parts:
  Part1 = Intel Edison Arduinobreakout
  R2 = Resistor [tolerance=±5% resistance=470 package="0402 [SMD]"]
  LED1 = smd LED [color="Red (633nm)" package="1206 [SMD]"]

nets:
  N1: Part1.D13/SCK, R2.Pin_0
  N2: Part1.GND, LED1.cathode
  N3: R2.Pin_1, LED1.anode
