# Fritzing sketch edison_schematics (saved by Fritzing 0.9.3b)
circuit board: 8.46667cm x 5.64444cm
breadboards: 1

parts:
  Part1 = Intel Edison Arduinobreakout
  R1 = Resistor [tolerance=±5% resistance=10k package="0402 [SMD]"]
  S1 = Pushbutton [package="[THT]"]

nets:
  N1: Part1.D12/MISO, R1.Pin_1, S1.Pin_3, S1.Pin_4
  N2: Part1.GND, S1.Pin_1, S1.Pin_2
  N3: Part1.5V, R1.Pin_0
