# Fritzing sketch edison_schematics (saved by Fritzing 0.9.3b)

parts:
  J1 = Basic Servo
  Part1 = Intel Edison Arduinobreakout

nets:
  GND: J1.gnd, Part1.GND
  VCC: J1.vcc, Part1.5V
  N1: J1.pulse, Part1.D6_PWM
