# Fritzing sketch rpi3_schematics_button (saved by Fritzing 0.9.3b)
circuit board: 8.46667cm x 5.64444cm
breadboards: 1

parts:
  Raspberry_Pi_1 = Raspberry Pi 3 [part_number=RPI-3-V1.2]
  R1 = Resistor [tolerance=±5% resistance=10k package="0402 [SMD]"]
  S1 = Pushbutton [package="[THT]"]

nets:
  N1: Raspberry_Pi_1.GND, S1.Pin_1, S1.Pin_2
  N2: Raspberry_Pi_1.GPIO21, R1.Pin_1, S1.Pin_3, S1.Pin_4
  N3: Raspberry_Pi_1.5V, R1.Pin_0
